# Fritzing sketch SmartWatchFritzing (saved by Fritzing 0.8.7b)
circuit board: 6.96816cm x 3.06841cm
breadboards: 1

parts:
  J2 = double row female pin header, 6 pins [form="♀ (female)"]
  TMP006 = female pin header, 7 pins [form="♀ (female)"]
  ADS1015 = female pin header, 9 pins [form="♀ (female)"]
  ADXL345 = female pin header, 10 pins [form="♀ (female)"]

nets:
  N1: J2.pin1, TMP006.pin1, ADS1015.pin1, ADXL345.pin1
  N2: J2.pin2, TMP006.pin3, ADS1015.pin8, ADXL345.pin4
  N3: J2.pin3, TMP006.pin4, ADS1015.pin9, ADXL345.pin3
  N4: J2.pin6, TMP006.pin2, ADS1015.pin3, ADXL345.pin2

notes:
  3V3
  SDA
  SCL
  5V
  GND
  VCC
  BTJ
